// Logisim project ALU_project.circ as structural Verilog: 11 circuits, main circuit main
module main (
  input  [1:0] Control,
  input  [13:0] A,
  input  [13:0] B,
  output [13:0] Result,
  output Zero,
  output Negative,
  output Overflow,
  output Carry
);

  L_14_bit_ALU l_14_bit_alu_1 (
    .A(A), .B(B), .Control0(Control[0]), .Control1(Control[1]), .Result(Result), .Zero(Zero),
    .Negative(Negative), .Overflow(Overflow), .Carry(Carry));
endmodule

// 14-bit AND
module L_14_bit_and (
  input  [13:0] A,
  input  [13:0] B,
  output [13:0] Result
);

  assign Result = A & B;  // AND_Gate and_1, 14 bits wide
endmodule

// 14-bit OR
module L_14_bit_OR (
  input  [13:0] A,
  input  [13:0] B,
  output [13:0] Result
);

  assign Result = A | B;  // OR_Gate or_1, 14 bits wide
endmodule

module Full_adder (
  input  Carry_in,
  input  A,
  input  B,
  output Result,
  output Carry_out
);

  wire and_1_out, and_2_out, xor_1_out;

  and and_1 (and_1_out, B, A);
  xor xor_1 (xor_1_out, A, B);
  or or_1 (Carry_out, and_1_out, and_2_out);
  and and_2 (and_2_out, xor_1_out, Carry_in);
  xor xor_2 (Result, Carry_in, xor_1_out);
endmodule

module L_14_bit_full_adder (
  input  Carry_in_c94f383c,
  input  A0,
  input  B0,
  input  A1,
  input  B1,
  input  A2,
  input  B2,
  input  A3,
  input  B3,
  input  A4,
  input  B4,
  input  A5,
  input  B5,
  input  A6,
  input  B6,
  input  A7,
  input  B7,
  input  A8,
  input  B8,
  input  A9,
  input  B9,
  input  A10,
  input  B10,
  input  A11,
  input  B11,
  input  A12,
  input  B12,
  input  A13,
  input  B13,
  output Result0,
  output Result1,
  output Result2,
  output Result3,
  output Result4,
  output Result5,
  output Result6,
  output Result7,
  output Result8,
  output Result9,
  output Result10,
  output Result11,
  output Result12,
  output Result13,
  output Carry
);

  wire full_adder_1_carry_out, full_adder_2_carry_out, full_adder_3_carry_out, full_adder_4_carry_out,
       full_adder_5_carry_out, full_adder_6_carry_out, full_adder_7_carry_out, full_adder_8_carry_out,
       full_adder_9_carry_out, full_adder_10_carry_out, full_adder_11_carry_out, full_adder_12_carry_out,
       full_adder_13_carry_out;

  Full_adder full_adder_1 (
    .A(A0), .B(B0), .Carry_in(Carry_in_c94f383c), .Carry_out(full_adder_1_carry_out), .Result(Result0));
  Full_adder full_adder_2 (
    .A(A1), .B(B1), .Carry_in(full_adder_1_carry_out), .Carry_out(full_adder_2_carry_out), .Result(Result1));
  Full_adder full_adder_3 (
    .A(A2), .B(B2), .Carry_in(full_adder_2_carry_out), .Carry_out(full_adder_3_carry_out), .Result(Result2));
  Full_adder full_adder_4 (
    .A(A3), .B(B3), .Carry_in(full_adder_3_carry_out), .Carry_out(full_adder_4_carry_out), .Result(Result3));
  Full_adder full_adder_5 (
    .A(A4), .B(B4), .Carry_in(full_adder_4_carry_out), .Carry_out(full_adder_5_carry_out), .Result(Result4));
  Full_adder full_adder_6 (
    .A(A5), .B(B5), .Carry_in(full_adder_5_carry_out), .Carry_out(full_adder_6_carry_out), .Result(Result5));
  Full_adder full_adder_7 (
    .A(A6), .B(B6), .Carry_in(full_adder_6_carry_out), .Carry_out(full_adder_7_carry_out), .Result(Result6));
  Full_adder full_adder_8 (
    .A(A7), .B(B7), .Carry_in(full_adder_7_carry_out), .Carry_out(full_adder_8_carry_out), .Result(Result7));
  Full_adder full_adder_9 (
    .A(A8), .B(B8), .Carry_in(full_adder_8_carry_out), .Carry_out(full_adder_9_carry_out), .Result(Result8));
  Full_adder full_adder_10 (
    .A(A9), .B(B9), .Carry_in(full_adder_9_carry_out), .Carry_out(full_adder_10_carry_out), .Result(Result9));
  Full_adder full_adder_11 (
    .A(A10), .B(B10), .Carry_in(full_adder_10_carry_out), .Carry_out(full_adder_11_carry_out),
    .Result(Result10));
  Full_adder full_adder_12 (
    .A(A11), .B(B11), .Carry_in(full_adder_11_carry_out), .Carry_out(full_adder_12_carry_out),
    .Result(Result11));
  Full_adder full_adder_13 (
    .A(A12), .B(B12), .Carry_in(full_adder_12_carry_out), .Carry_out(full_adder_13_carry_out),
    .Result(Result12));
  Full_adder full_adder_14 (.A(A13), .B(B13), .Carry_in(full_adder_13_carry_out), .Carry_out(Carry), .Result(Result13));
endmodule

// FA
module L_14_bit_full_adder_concise (
  input  Carry_in_c94f383c,
  input  [13:0] A,
  input  [13:0] B,
  output Carry,
  output [13:0] Result
);

  wire full_adder_1_carry_out, full_adder_2_carry_out, full_adder_3_carry_out, full_adder_4_carry_out,
       full_adder_5_carry_out, full_adder_6_carry_out, full_adder_7_carry_out, full_adder_8_carry_out,
       full_adder_9_carry_out, full_adder_10_carry_out, full_adder_11_carry_out, full_adder_12_carry_out,
       full_adder_13_carry_out;

  Full_adder full_adder_1 (
    .A(A[0]), .B(B[0]), .Carry_in(Carry_in_c94f383c), .Carry_out(full_adder_1_carry_out), .Result(Result[0]));
  Full_adder full_adder_2 (
    .A(A[1]), .B(B[1]), .Carry_in(full_adder_1_carry_out), .Carry_out(full_adder_2_carry_out),
    .Result(Result[1]));
  Full_adder full_adder_3 (
    .A(A[2]), .B(B[2]), .Carry_in(full_adder_2_carry_out), .Carry_out(full_adder_3_carry_out),
    .Result(Result[2]));
  Full_adder full_adder_4 (
    .A(A[3]), .B(B[3]), .Carry_in(full_adder_3_carry_out), .Carry_out(full_adder_4_carry_out),
    .Result(Result[3]));
  Full_adder full_adder_5 (
    .A(A[4]), .B(B[4]), .Carry_in(full_adder_4_carry_out), .Carry_out(full_adder_5_carry_out),
    .Result(Result[4]));
  Full_adder full_adder_6 (
    .A(A[5]), .B(B[5]), .Carry_in(full_adder_5_carry_out), .Carry_out(full_adder_6_carry_out),
    .Result(Result[5]));
  Full_adder full_adder_7 (
    .A(A[6]), .B(B[6]), .Carry_in(full_adder_6_carry_out), .Carry_out(full_adder_7_carry_out),
    .Result(Result[6]));
  Full_adder full_adder_8 (
    .A(A[7]), .B(B[7]), .Carry_in(full_adder_7_carry_out), .Carry_out(full_adder_8_carry_out),
    .Result(Result[7]));
  Full_adder full_adder_9 (
    .A(A[7]), .B(B[8]), .Carry_in(full_adder_8_carry_out), .Carry_out(full_adder_9_carry_out),
    .Result(Result[8]));
  Full_adder full_adder_10 (
    .A(A[9]), .B(B[9]), .Carry_in(full_adder_9_carry_out), .Carry_out(full_adder_10_carry_out),
    .Result(Result[9]));
  Full_adder full_adder_11 (
    .A(A[10]), .B(B[10]), .Carry_in(full_adder_10_carry_out), .Carry_out(full_adder_11_carry_out),
    .Result(Result[10]));
  Full_adder full_adder_12 (
    .A(A[11]), .B(B[11]), .Carry_in(full_adder_11_carry_out), .Carry_out(full_adder_12_carry_out),
    .Result(Result[11]));
  Full_adder full_adder_13 (
    .A(A[12]), .B(B[12]), .Carry_in(full_adder_12_carry_out), .Carry_out(full_adder_13_carry_out),
    .Result(Result[12]));
  Full_adder full_adder_14 (
    .A(A[13]), .B(B[13]), .Carry_in(full_adder_13_carry_out), .Carry_out(Carry), .Result(Result[13]));
endmodule

// L_14BITXOR
module L_14_bit_xor (
  input  Control,
  input  [13:0] B,
  output [13:0] Result
);

  wire [13:0] bit_extender_1_out;

  assign bit_extender_1_out = {{13{Control}}, Control};  // Bit_Extender bit_extender_1
  assign Result = bit_extender_1_out ^ B;  // XOR_Gate xor_1, 14 bits wide
endmodule

// 14-bit \nADD/SUB
module Add_sub (
  input  sub,
  input  [13:0] A,
  input  [13:0] B,
  output [13:0] Result,
  output Carry,
  output Overflow
);

  wire and_1_out, and_2_out, l_13th_bit_out_1_l_13th_bit_34f44a05, l_13th_bit_out_2_l_13th_bit_34f44a05,
       l_13th_bit_out_3_l_13th_bit_34f44a05, not_1_out, not_2_out, not_3_out;
  wire [13:0] l_14_bit_xor_1_result;

  L_13th_bit_out l_13th_bit_out_1 (.Input(A), .L_13th_bit_34f44a05(l_13th_bit_out_1_l_13th_bit_34f44a05));
  not not_1 (not_1_out, l_13th_bit_out_1_l_13th_bit_34f44a05);
  L_13th_bit_out l_13th_bit_out_2 (.Input(B), .L_13th_bit_34f44a05(l_13th_bit_out_2_l_13th_bit_34f44a05));
  not not_2 (not_2_out, l_13th_bit_out_2_l_13th_bit_34f44a05);
  L_14_bit_xor l_14_bit_xor_1 (.Control(sub), .B(B), .Result(l_14_bit_xor_1_result));
  L_14_bit_full_adder_concise l_14_bit_full_adder_concise_1 (
    .A(A), .B(l_14_bit_xor_1_result), .Carry_in_c94f383c(sub), .Result(Result), .Carry(Carry));
  L_13th_bit_out l_13th_bit_out_3 (.Input(Result), .L_13th_bit_34f44a05(l_13th_bit_out_3_l_13th_bit_34f44a05));
  not not_3 (not_3_out, l_13th_bit_out_3_l_13th_bit_34f44a05);
  and and_1 (and_1_out, not_3_out, l_13th_bit_out_2_l_13th_bit_34f44a05, l_13th_bit_out_1_l_13th_bit_34f44a05);
  and and_2 (and_2_out, l_13th_bit_out_3_l_13th_bit_34f44a05, not_2_out, not_1_out);
  or or_1 (Overflow, and_1_out, and_2_out);

  // Notes on the sheet:
  //   A13
  //   B13
  //   Result 13
endmodule

// 13th
module L_13th_bit_out (
  input  [13:0] Input,
  output L_13th_bit_34f44a05
);


  assign L_13th_bit_34f44a05 = Input[13];
endmodule

// Reduce-OR
module L_14_bit_reduce_or (
  input  [13:0] Input,
  output Output
);

  or or_1 (Output, Input[0], Input[1], Input[2], Input[3], Input[4], Input[5], Input[6], Input[8], Input[9], Input[10], Input[11], Input[12], Input[13], Input[7]);
endmodule

// 14-bit-ALU
module L_14_bit_ALU (
  input  Control0,
  input  Control1,
  input  [13:0] A,
  input  [13:0] B,
  output [13:0] Result,
  output Zero,
  output Negative,
  output Overflow,
  output Carry
);

  wire l_14_bit_reduce_or_1_output;
  wire [13:0] add_sub_1_result, l_14_bit_and_1_result, l_14_bit_or_1_result, multiplexer_1_out;

  L_14_bit_and l_14_bit_and_1 (.A(A), .B(B), .Result(l_14_bit_and_1_result));
  L_14_bit_OR l_14_bit_or_1 (.A(A), .B(B), .Result(l_14_bit_or_1_result));
  Add_sub add_sub_1 (.A(A), .B(B), .sub(Control0), .Overflow(Overflow), .Carry(Carry), .Result(add_sub_1_result));
  Multiplexer #(.width(14)) multiplexer_1 (
    .in0(l_14_bit_and_1_result), .in1(l_14_bit_or_1_result), .out(multiplexer_1_out), .sel(Control0));
  Multiplexer #(.width(14)) multiplexer_2 (
    .in0(multiplexer_1_out), .in1(add_sub_1_result), .out(Result), .sel(Control1));
  L_13th_bit_out l_13th_bit_out_1 (.Input(Result), .L_13th_bit_34f44a05(Negative));
  L_14_bit_reduce_or l_14_bit_reduce_or_1 (.Input(Result), .Output(l_14_bit_reduce_or_1_output));
  not not_1 (Zero, l_14_bit_reduce_or_1_output);
endmodule
