// Logisim project lab4assignmenthw.circ as structural Verilog: 1 circuit, main circuit main
module main (
  input  in_1,
  input  [13:0] in_2
);

  wire clock_1_out;
  wire [1:0] counter_1_q;
  wire [6:0] rom_1_data;
  wire [13:0] multiplexer_1_out, register_1_q, register_2_q, register_3_q, register_4_q;

  Counter #(.width(2), .max('h3)) counter_1 (
    .Q(counter_1_q), .clk(clock_1_out), .clr(in_1));  // open: load, D, count, carry
  Clock clock_1 (.out(clock_1_out));
  Multiplexer #(.select(3), .width(14), .enable("false")) multiplexer_1 (
    .in0(in_2), .in1(register_1_q), .in2(register_2_q), .in3(register_3_q), .in4(register_4_q),
    .out(multiplexer_1_out), .sel(rom_1_data[6:4]));  // open: in5, in6, in7
  ROM #(.addrWidth(2), .dataWidth(7)) rom_1 (.addr(counter_1_q), .data(rom_1_data));  // open: sel
  Register #(.width(14)) register_1 (
    .D(multiplexer_1_out), .en(rom_1_data[3]), .Q(register_1_q), .clk(clock_1_out), .clr(in_1));
  Register #(.width(14)) register_2 (
    .D(multiplexer_1_out), .en(rom_1_data[2]), .Q(register_2_q), .clk(clock_1_out), .clr(in_1));
  Register #(.width(14)) register_3 (
    .D(multiplexer_1_out), .en(rom_1_data[1]), .Q(register_3_q), .clk(clock_1_out), .clr(in_1));
  Register #(.width(14)) register_4 (
    .D(multiplexer_1_out), .en(rom_1_data[0]), .Q(register_4_q), .clk(clock_1_out), .clr(in_1));

  // Notes on the sheet:
  //   contents of rom_1 (hex, n*v repeats v):
  //   8 14 21 42
endmodule
